// Logisim project 4B.circ as structural Verilog: 1 circuit, main circuit main
module main (
  input  A,
  input  B,
  input  C,
  output F
);

  wire and_1_out, and_2_out, not_1_out;

  not not_1 (not_1_out, A);
  and and_1 (and_1_out, A, B);
  and and_2 (and_2_out, C, not_1_out);
  or or_1 (F, and_1_out, and_2_out);
endmodule
