// Logisim project 5A_HS.circ as structural Verilog: 1 circuit, main circuit main
module main (
  input  A,
  input  B,
  output Difference,
  output Borrow
);

  wire not_1_out;

  not not_1 (not_1_out, A);
  xor xor_1 (Difference, A, B);
  and and_1 (Borrow, not_1_out, A);
endmodule
