// Logisim project DEMUX.circ as structural Verilog: 1 circuit, main circuit main
module main (
  input  S1,
  input  S2,
  input  in_3,
  output out_4,
  output out_5,
  output out_6,
  output out_7
);

  wire not_1_out, not_2_out;

  not not_1 (not_1_out, S1);
  not not_2 (not_2_out, S2);
  and and_1 (out_4, in_3, not_1_out, not_2_out);
  and and_2 (out_5, in_3, not_1_out, S2);
  and and_3 (out_6, in_3, S1, not_2_out);
  and and_4 (out_7, in_3, S1, S2);
endmodule
